// Logisim project GshareGiven.circ as structural Verilog: 7 circuits, main circuit main
module main (
);

  wire Clock, Correct, CorrectPred, Done, gsharepredictor_1_takebranch, inputgen_1_branchtaken,
       inputgen_1_isbranch, IsPredBranchCorrect, IsPredCorrect, not_1_out;
  wire [31:0] CorrectPredBranch, gsharepredictor_1_predbranchdest, inputgen_1_branchdestaddress,
       inputgen_1_predpc, inputgen_1_updatepc;

  InputGen inputgen_1 (
    .Clock(Clock), .PredPC(inputgen_1_predpc), .UpdatePC(inputgen_1_updatepc),
    .IsBranch(inputgen_1_isbranch), .BranchTaken(inputgen_1_branchtaken),
    .BranchDestAddress(inputgen_1_branchdestaddress));
  GsharePredictor gsharepredictor_1 (
    .PredPC(inputgen_1_predpc), .UpdatePC(inputgen_1_updatepc), .IsBranch(inputgen_1_isbranch),
    .BranchTaken(inputgen_1_branchtaken), .BranchDestAddr(inputgen_1_branchdestaddress), .Clock(Clock),
    .TakeBranch(gsharepredictor_1_takebranch), .PredBranchDest(gsharepredictor_1_predbranchdest));
  Clock clock_1 (.out(Clock));
  // Probe on gsharepredictor_1_predbranchdest
  Test test_1 (
    .TakeBranch(gsharepredictor_1_takebranch), .PredBranchAddress(gsharepredictor_1_predbranchdest),
    .Clock(Clock), .IsPredCorrect(IsPredCorrect), .CorrectPred(CorrectPred),
    .IsPredBranchCorrect(IsPredBranchCorrect), .CorrectPredBranch(CorrectPredBranch), .Correct(Correct),
    .Done(Done));
  not not_1 (not_1_out, Done);
  Shift_Register #(.length(28)) shift_register_1 (
    .shift(not_1_out), .in(Correct), .clk(Clock));  // open: out, load, clr, d0, q0, d1, q1, d2, q2, d3, q3, d4, q4, d5, q5, d6, q6, d7, q7, d8, q8, d9, q9, d10, q10, d11, q11, d12, q12, d13, q13, d14, q14, d15, q15, d16, q16, d17, q17, d18, q18, d19, q19, d20, q20, d21, q21, d22, q22, d23, q23, d24, q24, d25, q25, d26, q26, d27, q27
  // Probe on IsPredCorrect
  // Probe on CorrectPred
  // Probe on IsPredBranchCorrect
  // Probe on CorrectPredBranch
  // Probe on Correct
  // Probe on Done
endmodule

module GsharePredictor (
  input  [31:0] PredPC,
  input  [31:0] UpdatePC,
  input  IsBranch,
  input  BranchTaken,
  input  [31:0] BranchDestAddr,
  input  Clock,
  output TakeBranch,
  output [31:0] PredBranchDest
);

  wire and_2_out, Clock_t, comparator_1_eq, comparator_1_gt, Count, CounterData, Load, not_1_out, TagData;
  wire [0:0] CtWrData;
  wire [1:0] BrHistData, counters_1_countdata, Index, oldIndex;
  wire [2:0] rom_1_data;
  wire [31:0] register_1_q, register_2_q, tagregisters_1_countdata;

  not not_1 (not_1_out, Clock);
  and and_1 (Clock_t, not_1_out, IsBranch);
  Register #(.width(32)) register_1 (.D(PredPC), .Q(register_1_q), .clk(Clock));  // open: en, clr
  Register #(.width(32)) register_2 (.D(BranchDestAddr), .Q(register_2_q), .clk(Clock));  // open: en, clr
  assign Index = PredPC[1:0] ^ BrHistData;  // XOR_Gate xor_1, 2 bits wide
  Counters counters_1 (
    .in_2(oldIndex), .in_3(Index), .in_4(Clock_t), .CountData(counters_1_countdata), .in_5(Count),
    .in_6({1'b0, CtWrData[0]}), .in_1(Load));
  Comparator #(.width(2), .mode("unsigned")) comparator_1 (
    .a(counters_1_countdata), .b(2'b10), .gt(comparator_1_gt), .eq(comparator_1_eq));  // open: lt
  TagRegisters tagregisters_1 (
    .in_1(oldIndex), .in_2(Index), .in_3(register_1_q), .in_4(Clock_t), .in_5(1'b1),
    .CountData(tagregisters_1_countdata));
  BranchDestRegs branchdestregs_1 (
    .in_1(oldIndex), .in_2(Index), .in_3(register_2_q), .in_4(Clock_t), .in_5(1'b1),
    .CountData(PredBranchDest));
  or or_1 (CounterData, comparator_1_gt, comparator_1_eq);
  Comparator #(.width(32), .mode("unsigned")) comparator_2 (
    .a(tagregisters_1_countdata), .b(PredPC), .eq(TagData));  // open: gt, lt
  Register #(.width(2)) register_3 (.D(Index), .Q(oldIndex), .clk(Clock));  // open: en, clr
  ROM #(.addrWidth(2), .dataWidth(3)) rom_1 (.addr({TagData, BranchTaken}), .data(rom_1_data));  // open: sel
  Register #(.width(1)) u_Count (.D(rom_1_data[2]), .Q(Count), .clk(Clock));  // open: en, clr
  Register #(.width(1)) u_Load (.D(rom_1_data[1]), .Q(Load), .clk(Clock));  // open: en, clr
  Register #(.width(1)) u_CtWrData (.D(rom_1_data[0]), .Q(CtWrData[0]), .clk(Clock));  // open: en, clr
  Register #(.width(2)) Branch_History_Register (
    .D({BrHistData[0], BranchTaken}), .Q(BrHistData), .clk(and_2_out));  // open: en, clr
  and and_2 (and_2_out, Clock, IsBranch);
  and and_3 (TakeBranch, CounterData, TagData, IsBranch);

  // Other names for the same wires on the sheet: BranchDestData[31:0] = PredBranchDest; clk = Clock

  // Notes on the sheet:
  //   Counter Control
  //   contents of rom_1 (hex, n*v repeats v):
  //   2 3 6 4
endmodule

module InputGen (
  input  Clock,
  output [31:0] PredPC,
  output [31:0] UpdatePC,
  output IsBranch,
  output BranchTaken,
  output [31:0] BranchDestAddress
);

  wire [7:0] counter_1_q;

  Counter #(.max('h1b), .ongoal("stay")) counter_1 (
    .count(1'b1), .Q(counter_1_q), .clk(Clock));  // open: load, D, carry, clr
  ROM #(.dataWidth(32)) rom_1 (.addr(counter_1_q), .data(PredPC));  // open: sel
  ROM #(.dataWidth(1)) rom_2 (.addr(counter_1_q), .data(IsBranch));  // open: sel
  ROM #(.dataWidth(1)) rom_3 (.addr(counter_1_q), .data(BranchTaken));  // open: sel
  ROM #(.dataWidth(32)) rom_4 (.addr(counter_1_q), .data(BranchDestAddress));  // open: sel

  assign UpdatePC = PredPC;

  // Notes on the sheet:
  //   Counter max count is 27 because there are only 28 instructions
  //   contents of rom_1 (hex, n*v repeats v):
  //   5*0 1 1 1 5 2 2 2 3 3 3 0 0 4
  //   contents of rom_2 (hex, n*v repeats v):
  //   8*1 0 8*1 0 10*1
  //   contents of rom_3 (hex, n*v repeats v):
  //   8*1 0 6*1 4*0 1 0 1 0 1 0 1 0 1
  //   contents of rom_4 (hex, n*v repeats v):
  //   5*60 5f 5f 5f 0 5 5 5 8 8 8 60 60 0 10*60
endmodule

module Test (
  input  TakeBranch,
  input  [31:0] PredBranchAddress,
  input  Clock,
  output IsPredCorrect,
  output CorrectPred,
  output IsPredBranchCorrect,
  output [31:0] CorrectPredBranch,
  output Correct,
  output Done
);

  wire comparator_1_eq, comparator_2_eq, DontCare, not_1_out;
  wire [7:0] Count;

  Counter #(.max('h1c), .ongoal("stay")) counter_1 (.count(1'b1), .Q(Count), .clk(Clock));  // open: load, D, carry, clr
  ROM #(.dataWidth(1)) rom_1 (.addr(Count), .data(CorrectPred));  // open: sel
  ROM #(.dataWidth(32)) rom_2 (.addr(Count), .data(CorrectPredBranch));  // open: sel
  ROM #(.dataWidth(1)) rom_3 (.addr(Count), .data(DontCare));  // open: sel
  not not_1 (not_1_out, CorrectPred);
  Comparator #(.width(1), .mode("unsigned")) comparator_1 (
    .a(TakeBranch), .b(CorrectPred), .eq(comparator_1_eq));  // open: gt, lt
  or or_1 (IsPredCorrect, comparator_1_eq, DontCare);
  Comparator #(.width(32), .mode("unsigned")) comparator_2 (
    .a(PredBranchAddress), .b(CorrectPredBranch), .eq(comparator_2_eq));  // open: gt, lt
  Comparator #(.mode("unsigned")) comparator_3 (.a(Count), .b(8'h1c), .eq(Done));  // open: gt, lt
  // Probe on Count
  or or_2 (IsPredBranchCorrect, comparator_2_eq, not_1_out, DontCare);
  and and_1 (Correct, IsPredCorrect, IsPredBranchCorrect);

  // Notes on the sheet:
  //   Correct Take Branch
  //   Correct Prediction Branch Address
  //   Don't Care
  //   contents of rom_1 (hex, n*v repeats v):
  //   4*0 1 0 0 1 0 0 0 1 0 0 1 1 9*0 1 0 1
  //   contents of rom_2 (hex, n*v repeats v):
  //   0 0 0 60 60 0 5f 5f 5f 60 5 5 60 8 8 60 5f 8 8 60 5 7*60
  //   contents of rom_3 (hex, n*v repeats v):
  //   8*0 1 8*0 1
endmodule

module Counters (
  input  in_1,
  input  [1:0] in_2,
  input  [1:0] in_3,
  input  in_4,
  input  in_5,
  input  [1:0] in_6,
  output [1:0] CountData
);

  wire Count0, Count1, Count2, Count3, Decrement_Load0, Decrement_Load1, Decrement_Load2, Decrement_Load3;
  wire [1:0] CntData0, CntData1, CntData2, CntData3;

  Demultiplexer #(.select(2), .enable("false")) demultiplexer_1 (
    .out0(Decrement_Load0), .out1(Decrement_Load1), .out2(Decrement_Load2), .out3(Decrement_Load3),
    .in(in_1), .sel(in_2));
  Demultiplexer #(.select(2), .enable("false")) demultiplexer_2 (
    .out0(Count0), .out1(Count1), .out2(Count2), .out3(Count3), .in(in_5), .sel(in_2));
  Counter #(.width(2), .max('h3), .ongoal("stay")) counter_1 (
    .load(Decrement_Load0), .D(in_6), .count(Count0), .Q(CntData0), .clk(in_4));  // open: carry, clr
  Counter #(.width(2), .max('h3), .ongoal("stay")) counter_2 (
    .load(Decrement_Load1), .D(in_6), .count(Count1), .Q(CntData1), .clk(in_4));  // open: carry, clr
  Counter #(.width(2), .max('h3), .ongoal("stay")) counter_3 (
    .load(Decrement_Load2), .D(in_6), .count(Count2), .Q(CntData2), .clk(in_4));  // open: carry, clr
  Counter #(.width(2), .max('h3), .ongoal("stay")) counter_4 (
    .load(Decrement_Load3), .D(in_6), .count(Count3), .Q(CntData3), .clk(in_4));  // open: carry, clr
  Multiplexer #(.select(2), .width(2), .enable("false")) multiplexer_1 (
    .in0(CntData0), .in1(CntData1), .in2(CntData2), .in3(CntData3), .out(CountData), .sel(in_3));

  // Other names for the same wires on the sheet: clock = in_4; Decrement_Load = in_1; ReadAddress[1:0] = in_3;
  //   WrCnt = in_5; WriteAddress[1:0] = in_2; WriteData[1:0] = in_6
endmodule

module TagRegisters (
  input  [1:0] in_1,
  input  [1:0] in_2,
  input  [31:0] in_3,
  input  in_4,
  input  in_5,
  output [31:0] CountData
);

  wire WrTag0, WrTag1, WrTag2, WrTag3;
  wire [31:0] TagData0, TagData1, TagData3, TagtData2;

  Demultiplexer #(.select(2), .enable("false")) demultiplexer_1 (
    .out0(WrTag0), .out1(WrTag1), .out2(WrTag2), .out3(WrTag3), .in(in_5), .sel(in_1));
  Register #(.width(32)) register_1 (.D(in_3), .en(WrTag0), .Q(TagData0), .clk(in_4));  // open: clr
  Register #(.width(32)) register_2 (.D(in_3), .en(WrTag1), .Q(TagData1), .clk(in_4));  // open: clr
  Register #(.width(32)) register_3 (.D(in_3), .en(WrTag2), .Q(TagtData2), .clk(in_4));  // open: clr
  Register #(.width(32)) register_4 (.D(in_3), .en(WrTag3), .Q(TagData3), .clk(in_4));  // open: clr
  Multiplexer #(.select(2), .width(32), .enable("false")) multiplexer_1 (
    .in0(TagData0), .in1(TagData1), .in2(TagtData2), .in3(TagData3), .out(CountData), .sel(in_2));

  // Other names for the same wires on the sheet: clock = in_4; ReadAddress[1:0] = in_2; WriteAddress[1:0] = in_1;
  //   WriteData[31:0] = in_3; WrTag = in_5
endmodule

module BranchDestRegs (
  input  [1:0] in_1,
  input  [1:0] in_2,
  input  [31:0] in_3,
  input  in_4,
  input  in_5,
  output [31:0] CountData
);

  wire WrTag0, WrTag1, WrTag2, WrTag3;
  wire [31:0] TagData0, TagData1, TagData3, TagtData2;

  Demultiplexer #(.select(2), .enable("false")) demultiplexer_1 (
    .out0(WrTag0), .out1(WrTag1), .out2(WrTag2), .out3(WrTag3), .in(in_5), .sel(in_1));
  Register #(.width(32)) register_1 (.D(in_3), .en(WrTag0), .Q(TagData0), .clk(in_4));  // open: clr
  Register #(.width(32)) register_2 (.D(in_3), .en(WrTag1), .Q(TagData1), .clk(in_4));  // open: clr
  Register #(.width(32)) register_3 (.D(in_3), .en(WrTag2), .Q(TagtData2), .clk(in_4));  // open: clr
  Register #(.width(32)) register_4 (.D(in_3), .en(WrTag3), .Q(TagData3), .clk(in_4));  // open: clr
  Multiplexer #(.select(2), .width(32), .enable("false")) multiplexer_1 (
    .in0(TagData0), .in1(TagData1), .in2(TagtData2), .in3(TagData3), .out(CountData), .sel(in_2));

  // Other names for the same wires on the sheet: clock = in_4; ReadAddress[1:0] = in_2; WriteAddress[1:0] = in_1;
  //   WriteData[31:0] = in_3; WrTag = in_5
endmodule
