// Logisim project PipelinedMipsGiven.circ as structural Verilog: 11 circuits, main circuit main
module main (
);

  wire alu_1_zero, and_2_out, and_3_out, Branch, Branch_2_q, Bubble, Clear_Decode, clock, comparator_1_eq,
       EX_Branch, EX_J_B, EX_Jump, EX_MemRead, EX_MemWrite, EX_RegWrite, F_D_Write, Instr_2_q, Instr_3_q, JR,
       Jump, M_Branch, M_JR, M_Jump, M_MemRead, M_MemWrite, M_RegWrite, MemRead, MemWrite,
       mfwdcontrol_1_out_7, not_1_out, not_2_out, or_1_out, or_2_out, or_4_out, PC_Write, register_1_q,
       register_2_q, register_3_q, RegWrite, WB_RegWrite;
  wire [0:0] and_1_out;
  wire [1:0] A, ALUOp, ALUSrcB, B, EX_ALUOp, EX_ALUSrcB, EX_MemtoReg, EX_RegDst, M_MemtoReg, MemtoReg,
       RegDest, WB_MemtoReg;
  wire [2:0] ALUCtl;
  wire [4:0] _10_6, _20_16, EX__15_11, EX__20_16, M__15_11, M__20_16, M_RegDst, multiplexer_15_out,
       RegDst_2_q;
  wire [5:0] EX_Opcode, M_Function, M_Opcode, multiplexer_7_out, Opcode;
  wire [7:0] PC_2_q_2;
  wire [12:0] rom_2_data;
  wire [15:0] _15_0;
  wire [25:0] EX__25_0;
  wire [25:21] _25_0;
  wire [31:0] adder_1_out, adder_2_out, alu_1_aluresult, bit_extender_1_out, Data_q, EX_PC, EX_Rs, EX_SE,
       M_ALUR, multiplexer_1_out, multiplexer_3_out, multiplexer_4_out, multiplexer_5_out,
       multiplexer_10_out, multiplexer_11_out, multiplexer_12_out, multiplexer_13_out, multiplexer_14_out,
       nPC, PC_2_q, PC_4_q, ram_1_data, RD1_2_q, RD2, RD2_2_q, ReadData_q, regfile_1_rddata1,
       regfile_1_rddata2, register_5_q, rom_1_data, shifter_1_out, WB_WrData;

  // Probe on {PC_2_q[31:10], PC_2_q_2, PC_2_q[1:0]}
  Register #(.width(1), .trigger("falling")) register_1 (.D(PC_Write), .Q(register_1_q), .clk(clock));  // open: en, clr
  Multiplexer #(.width(32)) multiplexer_1 (
    .in0(nPC), .in1({PC_2_q[31:10], PC_2_q_2, PC_2_q[1:0]}), .out(multiplexer_1_out), .sel(register_1_q));  // open: en
  Register #(.width(32)) PC_2 (
    .D(multiplexer_1_out), .Q({PC_2_q[31:10], PC_2_q_2, PC_2_q[1:0]}), .clk(clock));  // open: en, clr
  not not_1 (not_1_out, EX_J_B);
  Multiplexer #(.width(32)) multiplexer_2 (
    .in0(multiplexer_13_out), .in1(adder_1_out), .out(nPC), .sel(not_1_out));  // open: en
  ROM #(.dataWidth(32)) rom_1 (.addr(PC_2_q_2), .data(rom_1_data));  // open: sel
  Adder #(.width(32)) adder_1 (
    .a(32'h4), .b({PC_2_q[31:10], PC_2_q_2, PC_2_q[1:0]}), .out(adder_1_out));  // open: cin, cout
  Register #(.width(1), .trigger("falling")) register_2 (
    .D(F_D_Write), .Q(register_2_q), .clk(clock));  // open: en, clr
  // Probe on multiplexer_4_out
  Clock clock_1 (.out(clock));
  Multiplexer #(.width(32)) multiplexer_3 (
    .in0(adder_1_out), .in1(PC_4_q), .out(multiplexer_3_out), .sel(register_2_q));  // open: en
  Multiplexer #(.width(32)) multiplexer_4 (
    .in0(rom_1_data), .in1({32{1'b0}}), .out(multiplexer_4_out), .sel(Clear_Decode));  // open: en
  Register #(.width(32)) PC_4 (.D(multiplexer_3_out), .Q(PC_4_q), .clk(clock));  // open: en, clr
  Register #(.width(1), .trigger("falling")) register_3 (
    .D(F_D_Write), .Q(register_3_q), .clk(clock));  // open: en, clr
  Multiplexer #(.width(32)) multiplexer_5 (
    .in0(multiplexer_4_out), .in1({Opcode, _25_0, _20_16, _15_0[15:11], _10_6, _15_0[5:0]}),
    .out(multiplexer_5_out), .sel(register_3_q));  // open: en
  Register #(.width(32)) Instr (
    .D(multiplexer_5_out), .Q({Opcode, _25_0, _20_16, _15_0[15:11], _10_6, _15_0[5:0]}), .clk(clock));  // open: en, clr
  ROM #(.addrWidth(6), .dataWidth(13)) rom_2 (.addr(Opcode), .data(rom_2_data));  // open: sel
  // Probe on _25_0
  // Probe on _20_16
  // Probe on _15_0[15:11]
  // Probe on {_15_0[15:11], _10_6, _15_0[5:0]}
  Register #(.width(1), .trigger("falling")) Instr_2 (.D(Bubble), .Q(Instr_2_q), .clk(clock));  // open: en, clr
  Multiplexer #(.width(13)) multiplexer_6 (
    .in0(rom_2_data), .in1({13{1'b0}}),
    .out({MemRead, MemWrite, ALUSrcB, ALUOp, Branch, Jump, RegWrite, MemtoReg, RegDest}), .sel(Instr_2_q));  // open: en
  Comparator #(.width(6)) comparator_1 (.a(_15_0[5:0]), .b(6'b001000), .eq(comparator_1_eq));  // open: gt, lt
  HazardDetection hazarddetection_1 (
    .out_9(PC_Write), .out_10(F_D_Write), .in_2(_25_0), .in_4(_20_16), .out_12(Clear_Decode),
    .in_1(EX_MemRead), .out_11(Bubble), .in_3(EX__20_16), .in_5(EX_J_B), .in_6(MemRead), .in_7(or_1_out),
    .in_8(clock));
  Register #(.width(1), .trigger("falling")) Instr_3 (.D(Bubble), .Q(Instr_3_q), .clk(clock));  // open: en, clr
  Multiplexer #(.width(6)) multiplexer_7 (
    .in0(_15_0[5:0]), .in1({6{1'b0}}), .out(multiplexer_7_out), .sel(Instr_3_q));  // open: en
  // Probe on RegDst_2_q
  or or_1 (or_1_out, comparator_1_eq, Branch, Jump);
  RegFile regfile_1 (
    .WrAddr(RegDst_2_q), .WrData(WB_WrData), .WrReg(WB_RegWrite), .RdAddr1(_25_0), .RdAddr2(_20_16),
    .RdData1(regfile_1_rddata1), .RdData2(regfile_1_rddata2), .Clock(clock));
  assign bit_extender_1_out = {{16{_15_0[15]}}, {_15_0[15:11], _10_6, _15_0[5:0]}};  // Bit_Extender bit_extender_1
  // Probe on WB_WrData
  // Probe on regfile_1_rddata1
  // Probe on regfile_1_rddata2
  Register #(.width(32)) PC_4_2 (.D(PC_4_q), .Q(EX_PC), .clk(clock));  // open: en, clr
  Register #(.width(6)) EX_Signals (
    .D({ALUSrcB, ALUOp, RegDest}), .Q({EX_ALUSrcB, EX_ALUOp, EX_RegDst}), .clk(clock));  // open: en, clr
  Register #(.width(4)) Mem_Signals (
    .D({MemRead, MemWrite, Branch, Jump}), .Q({EX_MemRead, EX_MemWrite, EX_Branch, EX_Jump}), .clk(clock));  // open: en, clr
  Register #(.width(3)) WB_Signals (
    .D({MemtoReg, RegWrite}), .Q({EX_MemtoReg, EX_RegWrite}), .clk(clock));  // open: en, clr
  Register #(.width(32)) RD1_2 (.D(regfile_1_rddata1), .Q(RD1_2_q), .clk(clock));  // open: en, clr
  Register #(.width(32)) RD2_2 (.D(regfile_1_rddata2), .Q(RD2_2_q), .clk(clock));  // open: en, clr
  Register #(.width(32)) SE (.D(bit_extender_1_out), .Q(EX_SE), .clk(clock));  // open: en, clr
  Register #(.width(27)) Other (
    .D({multiplexer_7_out, _10_6, _15_0[15:11], _20_16, Opcode}),
    .Q({EX__25_0[5:0], EX__25_0[10:6], EX__15_11, EX__20_16, EX_Opcode}), .clk(clock));  // open: en, clr
  Register #(.width(5)) register_4 (.D(_25_0), .Q(EX__25_0[25:21]), .clk(clock));  // open: en, clr
  Multiplexer #(.select(2), .width(32)) multiplexer_8 (
    .in0(RD1_2_q), .in1(M_ALUR), .in2(WB_WrData), .out(EX_Rs), .sel(A));  // open: in3, en
  Multiplexer #(.select(2), .width(32)) multiplexer_9 (
    .in0(RD2_2_q), .in1(M_ALUR), .in2(WB_WrData), .out(RD2), .sel(B));  // open: in3, en
  FwdControl fwdcontrol_1 (
    .in_1(EX__25_0[25:21]), .in_3(EX__20_16), .in_2(M_RegWrite), .in_4(M_RegDst), .in_5(RegDst_2_q),
    .in_6(WB_RegWrite), .out_7(A), .out_8(B));
  // Probe on nothing
  ALUControl alucontrol_1 (.in_1(EX_Opcode), .in_2(EX__25_0[5:0]), .in_3(EX_ALUOp), .out_4(ALUCtl), .out_5(JR));
  // Probe on JR
  Shifter #(.width(32)) shifter_1 (.in(EX_SE), .\dist (5'b00010), .out(shifter_1_out));
  Multiplexer #(.width(32)) multiplexer_10 (
    .in0(EX_Rs), .in1({32{1'b0}}), .out(multiplexer_10_out), .sel(EX_Jump));  // open: en
  Multiplexer #(.select(2), .width(32)) multiplexer_11 (
    .in0(RD2), .in1(EX_SE), .in2(EX_PC), .out(multiplexer_11_out), .sel(EX_ALUSrcB));  // open: in3, en
  Adder #(.width(32)) adder_2 (.a(EX_PC), .b(shifter_1_out), .out(adder_2_out));  // open: cin, cout
  // Probe on multiplexer_11_out
  // Probe on RegWrite
  Multiplexer #(.width(32)) multiplexer_12 (
    .in0(adder_2_out), .in1({EX_PC[31:28], EX__25_0[25:21], EX__20_16, EX__15_11, EX__25_0[10:0], 2'b00}),
    .out(multiplexer_12_out), .sel(EX_Jump));  // open: en
  // Probe on multiplexer_10_out
  MFwdControl mfwdcontrol_1 (
    .in_3(M__15_11), .in_4(M__20_16), .in_5(EX__20_16), .in_6(M_Opcode), .in_1(M_MemtoReg),
    .in_2(M_RegWrite), .out_7(mfwdcontrol_1_out_7));
  Multiplexer #(.width(32)) multiplexer_13 (
    .in0(multiplexer_12_out), .in1(EX_Rs), .out(multiplexer_13_out), .sel(JR));  // open: en
  or or_2 (or_2_out, JR, EX_Jump);
  ALU alu_1 (
    .ALUCtl(ALUCtl), .A(multiplexer_10_out), .B(multiplexer_11_out), .ALUResult(alu_1_aluresult),
    .Zero(alu_1_zero), .Shamt(EX__25_0[10:6]));  // open: Overflow
  // Probe on Branch
  and and_1 (and_1_out[0], EX_RegWrite, not_2_out);
  not not_2 (not_2_out, JR);
  or or_3 (EX_J_B, or_2_out, and_2_out);
  and and_2 (and_2_out, EX_Branch, alu_1_zero);
  // Probe on alu_1_aluresult
  Multiplexer #(.width(32)) multiplexer_14 (
    .in0(RD2), .in1(M_ALUR), .out(multiplexer_14_out), .sel(mfwdcontrol_1_out_7));  // open: en
  // Probe on Jump
  Register #(.width(5)) Mem_Signals_2 (
    .D({EX_MemRead, EX_MemWrite, EX_Branch, EX_Jump, JR}),
    .Q({M_MemRead, M_MemWrite, M_Branch, M_Jump, M_JR}), .clk(clock));  // open: en, clr
  Register #(.width(3)) WB_Signals_2 (
    .D({EX_MemtoReg, and_1_out[0]}), .Q({M_MemtoReg, M_RegWrite}), .clk(clock));  // open: en, clr
  Register #(.width(1)) Branch_2 (.D(alu_1_zero), .Q(Branch_2_q));  // open: en, clk, clr
  Register #(.width(32)) Address (.D(alu_1_aluresult), .Q(M_ALUR), .clk(clock));  // open: en, clr
  Register #(.width(32)) Data (.D(multiplexer_14_out), .Q(Data_q), .clk(clock));  // open: en, clr
  Register #(.width(22)) Other_2 (
    .D({EX_Opcode, EX__20_16, EX__15_11, EX__25_0[5:0]}), .Q({M_Opcode, M__20_16, M__15_11, M_Function}),
    .clk(clock));  // open: en, clr
  Register #(.width(5)) RegDst (.D(multiplexer_15_out), .Q(M_RegDst), .clk(clock));  // open: en, clr
  Multiplexer #(.select(2), .width(5)) multiplexer_15 (
    .in0(EX__20_16), .in1(EX__15_11), .in2({5{1'b1}}), .in3({5{1'b1}}), .out(multiplexer_15_out),
    .sel(EX_RegDst));  // open: en
  or or_4 (or_4_out, M_JR, M_Jump);
  and and_3 (and_3_out, M_Branch, Branch_2_q);
  // Probe on M_MemWrite
  // OR_Gate or_5 has open pins: in0=or_4_out, in1=and_3_out, out=open
  // Probe on Data_q
  RAM #(.dataWidth(32), .bus("separate")) ram_1 (
    .addr(M_ALUR[7:0]), .din(Data_q), .data(ram_1_data), .str(M_MemWrite), .clk(clock), .ld(M_MemRead));  // open: sel, clr
  // Probe on ram_1_data
  Register #(.width(3)) WB_Signals_3 (
    .D({M_MemtoReg, M_RegWrite}), .Q({WB_MemtoReg, WB_RegWrite}), .clk(clock));  // open: en, clr
  Register #(.width(32)) register_5 (.D(M_ALUR), .Q(register_5_q), .clk(clock));  // open: en, clr
  Register #(.width(32)) ReadData (.D(ram_1_data), .Q(ReadData_q), .clk(clock));  // open: en, clr
  Register #(.width(5)) RegDst_2 (.D(M_RegDst), .Q(RegDst_2_q), .clk(clock));  // open: en, clr
  Multiplexer #(.select(2), .width(32)) multiplexer_16 (
    .in0(register_5_q), .in1(ReadData_q), .in2(register_5_q), .out(WB_WrData), .sel(WB_MemtoReg));  // open: in3, en

  // Other names for the same wires on the sheet: _25_0[20:0] = {_20_16, _15_0[15:11], _10_6, _15_0[5:0]};
  //   _15_11[4:0] = _15_0[15:11]; _15_0[10:6] = _10_6; Shamt[4:0] = EX__25_0[10:6]; EX__25_21[4:0] = EX__25_0[25:21];
  //   EX_Function[5:0] = EX__25_0[5:0]; EX__25_0[20:11] = {EX__20_16, EX__15_11}; Function[5:0] = _15_0[5:0];
  //   _25_21[4:0] = _25_0; IF_PCSrc = EX_J_B

  // Notes on the sheet:
  //   contents of rom_1 (hex, n*v repeats v):
  //   34010001 211020 221827 2064000e 232824 aca4000a 8ca6000a c43824 10e10003 c7402a 11080001 201cffff
  //   8c0a000a ad4afff7 8c0a000a 1141fffc c000012 201bffff 23ff0018 ac1f0000 8c150000 2a00008 201affff
  //   8000017 20230000 20440000 20050001 a03020 10040006 ac650000 20840001 20630001 862022 10040001
  //   8000000 3e00008
  //   PC Control Signals
  //   contents of rom_2 (hex, n*v repeats v):
  //   111 0 421 43a c1 0 0 0 390 0 0 0 390 390 21*0 1214 7*0 a00
  //   [31-26]
  //   [5-0]
  //   Rs
  //   Rt
  //   Rd
endmodule

module _32bit (
  input  Add_Sub_control,
  input  [31:0] in_2,
  input  [31:0] in_3,
  output [31:0] out_4,
  output carry_out
);

  wire adder_1_cout, subtractor_1_bout;
  wire [31:0] adder_1_out, subtractor_1_out;

  Adder #(.width(32)) adder_1 (.a(in_2), .b(in_3), .out(adder_1_out), .cout(adder_1_cout));  // open: cin
  Subtractor #(.width(32)) subtractor_1 (
    .a(in_2), .b(in_3), .out(subtractor_1_out), .bout(subtractor_1_bout));  // open: bin
  Multiplexer #(.width(32), .enable("false")) multiplexer_1 (
    .in0(adder_1_out), .in1(subtractor_1_out), .out(out_4), .sel(Add_Sub_control));
  Multiplexer #(.enable("false")) multiplexer_2 (
    .in0(adder_1_cout), .in1(subtractor_1_bout), .out(carry_out), .sel(Add_Sub_control));
endmodule

module ALU (
  input  [2:0] ALUCtl,
  input  [31:0] A,
  input  [31:0] B,
  input  [4:0] Shamt,
  output [31:0] ALUResult,
  output Zero,
  output Overflow
);

  wire and_2_out, and_3_out, comparator_1_lt, not_1_out, not_2_out, not_3_out, or_2_out;
  wire [31:0] Add, And, LessThan, Nor, Or, ShiftLeft, ShiftRight, Sub;

  Adder #(.width(32)) adder_1 (.a(A), .b(B), .out(Add));  // open: cin, cout
  Subtractor #(.width(32)) subtractor_1 (.a(A), .b(B), .out(Sub));  // open: bin, bout
  assign And = A & B;  // AND_Gate and_1, 32 bits wide
  assign Or = A | B;  // OR_Gate or_1, 32 bits wide
  assign Nor = ~(A | B);  // NOR_Gate nor_1, 32 bits wide
  Comparator #(.width(32)) comparator_1 (.a(A), .b(B), .lt(comparator_1_lt));  // open: gt, eq
  assign LessThan = {{31{1'b0}}, comparator_1_lt};  // Bit_Extender bit_extender_1
  Shifter #(.width(32)) shifter_1 (.in(B), .\dist (Shamt), .out(ShiftLeft));
  Shifter #(.width(32), .shift("lr")) shifter_2 (.in(B), .\dist (Shamt), .out(ShiftRight));
  not not_1 (not_1_out, ALUCtl[2]);
  not not_2 (not_2_out, ALUCtl[0]);
  not not_3 (not_3_out, ALUCtl[1]);
  Multiplexer #(.select(3), .width(32), .enable("false")) multiplexer_1 (
    .in0(LessThan), .in1(Sub), .in2(Nor), .in3(And), .in4(Add), .in5(Or), .in6(ShiftLeft), .in7(ShiftRight),
    .out(ALUResult), .sel(ALUCtl));
  and and_2 (and_2_out, not_2_out, not_3_out, ALUCtl[2]);
  and and_3 (and_3_out, not_2_out, ALUCtl[1], not_1_out);
  Overflow overflow_1 (
    .Add(and_2_out), .Sub(and_3_out), .ASign(A[31]), .BSign(B[31]), .ResultSign(ALUResult[31]),
    .Overflow(Overflow));
  not not_4 (Zero, or_2_out);
  or or_2 (or_2_out, ALUResult[0], ALUResult[1], ALUResult[2], ALUResult[3], ALUResult[4], ALUResult[5], ALUResult[6], ALUResult[7], ALUResult[8], ALUResult[9], ALUResult[10], ALUResult[11], ALUResult[12], ALUResult[13], ALUResult[14], ALUResult[15], ALUResult[16], ALUResult[17], ALUResult[18], ALUResult[19], ALUResult[20], ALUResult[21], ALUResult[22], ALUResult[23], ALUResult[24], ALUResult[25], ALUResult[26], ALUResult[27], ALUResult[28], ALUResult[29], ALUResult[30], ALUResult[31]);

  // Other names for the same wires on the sheet: ASign = A[31]; ResultSign = ALUResult[31]; BSign = B[31]
endmodule

module RegFile (
  input  [4:0] WrAddr,
  input  [31:0] WrData,
  input  WrReg,
  input  [4:0] RdAddr1,
  input  [4:0] RdAddr2,
  input  Clock,
  output [31:0] RdData1,
  output [31:0] RdData2
);

  wire and_1_out, and_2_out, comparator_1_eq, comparator_2_eq, comparator_3_eq, comparator_4_eq, not_1_out,
       not_2_out, WrReg0, WrReg1, WrReg2, WrReg3, WrReg4, WrReg5, WrReg6, WrReg7, WrReg8, WrReg9, WrReg10,
       WrReg11, WrReg12, WrReg13, WrReg14, WrReg15, WrReg16, WrReg17, WrReg18, WrReg19, WrReg20, WrReg21,
       WrReg22, WrReg23, WrReg24, WrReg25, WrReg26, WrReg27, WrReg28, WrReg29, WrReg30, WrReg31;
  wire [31:0] multiplexer_1_out, multiplexer_2_out, RegData1, RegData2, RegData3, RegData4, RegData5,
       RegData6, RegData7, RegData8, RegData9, RegData10, RegData11, RegData12, RegData13, RegData14,
       RegData15, RegData16, RegData17, RegData18, RegData19, RegData20, RegData21, RegData22, RegData23,
       RegData24, RegData25, RegData26, RegData27, RegData28, RegData29, RegData30, RegData31;

  Demultiplexer #(.select(5), .enable("false")) demultiplexer_1 (
    .out0(WrReg0), .out1(WrReg1), .out2(WrReg2), .out3(WrReg3), .out4(WrReg4), .out5(WrReg5), .out6(WrReg6),
    .out7(WrReg7), .out8(WrReg8), .out9(WrReg9), .out10(WrReg10), .out11(WrReg11), .out12(WrReg12),
    .out13(WrReg13), .out14(WrReg14), .out15(WrReg15), .out16(WrReg16), .out17(WrReg17), .out18(WrReg18),
    .out19(WrReg19), .out20(WrReg20), .out21(WrReg21), .out22(WrReg22), .out23(WrReg23), .out24(WrReg24),
    .out25(WrReg25), .out26(WrReg26), .out27(WrReg27), .out28(WrReg28), .out29(WrReg29), .out30(WrReg30),
    .out31(WrReg31), .in(WrReg), .sel(WrAddr));
  Register #(.width(32)) Reg4 (.D(WrData), .en(WrReg4), .Q(RegData4), .clk(Clock));  // open: clr
  Register #(.width(32)) Reg8 (.D(WrData), .en(WrReg8), .Q(RegData8), .clk(Clock));  // open: clr
  Register #(.width(32)) Reg12 (.D(WrData), .en(WrReg12), .Q(RegData12), .clk(Clock));  // open: clr
  Register #(.width(32)) Reg16 (.D(WrData), .en(WrReg16), .Q(RegData16), .clk(Clock));  // open: clr
  Register #(.width(32)) Reg20 (.D(WrData), .en(WrReg20), .Q(RegData20), .clk(Clock));  // open: clr
  Register #(.width(32)) Reg24 (.D(WrData), .en(WrReg24), .Q(RegData24), .clk(Clock));  // open: clr
  Register #(.width(32)) Reg28 (.D(WrData), .en(WrReg28), .Q(RegData28), .clk(Clock));  // open: clr
  Register #(.width(32)) Reg1 (.D(WrData), .en(WrReg1), .Q(RegData1), .clk(Clock));  // open: clr
  Register #(.width(32)) Reg5 (.D(WrData), .en(WrReg5), .Q(RegData5), .clk(Clock));  // open: clr
  Register #(.width(32)) Reg9 (.D(WrData), .en(WrReg9), .Q(RegData9), .clk(Clock));  // open: clr
  Register #(.width(32)) Reg13 (.D(WrData), .en(WrReg13), .Q(RegData13), .clk(Clock));  // open: clr
  Register #(.width(32)) Reg17 (.D(WrData), .en(WrReg17), .Q(RegData17), .clk(Clock));  // open: clr
  Register #(.width(32)) Reg21 (.D(WrData), .en(WrReg21), .Q(RegData21), .clk(Clock));  // open: clr
  Register #(.width(32)) Reg25 (.D(WrData), .en(WrReg25), .Q(RegData25), .clk(Clock));  // open: clr
  Register #(.width(32)) Reg29 (.D(WrData), .en(WrReg29), .Q(RegData29), .clk(Clock));  // open: clr
  Register #(.width(32)) Reg2 (.D(WrData), .en(WrReg2), .Q(RegData2), .clk(Clock));  // open: clr
  Register #(.width(32)) Reg6 (.D(WrData), .en(WrReg6), .Q(RegData6), .clk(Clock));  // open: clr
  Register #(.width(32)) Reg10 (.D(WrData), .en(WrReg10), .Q(RegData10), .clk(Clock));  // open: clr
  Register #(.width(32)) Reg14 (.D(WrData), .en(WrReg14), .Q(RegData14), .clk(Clock));  // open: clr
  Register #(.width(32)) Reg18 (.D(WrData), .en(WrReg18), .Q(RegData18), .clk(Clock));  // open: clr
  Register #(.width(32)) Reg22 (.D(WrData), .en(WrReg22), .Q(RegData22), .clk(Clock));  // open: clr
  Register #(.width(32)) Reg26 (.D(WrData), .en(WrReg26), .Q(RegData26), .clk(Clock));  // open: clr
  Register #(.width(32)) Reg30 (.D(WrData), .en(WrReg30), .Q(RegData30), .clk(Clock));  // open: clr
  Register #(.width(32)) Reg3 (.D(WrData), .en(WrReg3), .Q(RegData3), .clk(Clock));  // open: clr
  Register #(.width(32)) Reg7 (.D(WrData), .en(WrReg7), .Q(RegData7), .clk(Clock));  // open: clr
  Register #(.width(32)) Reg11 (.D(WrData), .en(WrReg11), .Q(RegData11), .clk(Clock));  // open: clr
  Register #(.width(32)) Reg15 (.D(WrData), .en(WrReg15), .Q(RegData15), .clk(Clock));  // open: clr
  Register #(.width(32)) Reg19 (.D(WrData), .en(WrReg19), .Q(RegData19), .clk(Clock));  // open: clr
  Register #(.width(32)) Reg23 (.D(WrData), .en(WrReg23), .Q(RegData23), .clk(Clock));  // open: clr
  Register #(.width(32)) Reg27 (.D(WrData), .en(WrReg27), .Q(RegData27), .clk(Clock));  // open: clr
  Register #(.width(32)) Reg31 (.D(WrData), .en(WrReg31), .Q(RegData31), .clk(Clock));  // open: clr
  Multiplexer #(.select(5), .width(32), .enable("false")) multiplexer_1 (
    .in0({32{1'b0}}), .in1(RegData1), .in2(RegData2), .in3(RegData3), .in4(RegData4), .in5(RegData5),
    .in6(RegData6), .in7(RegData7), .in8(RegData8), .in9(RegData9), .in10(RegData10), .in11(RegData11),
    .in12(RegData12), .in13(RegData13), .in14(RegData14), .in15(RegData15), .in16(RegData16),
    .in17(RegData17), .in18(RegData18), .in19(RegData19), .in20(RegData20), .in21(RegData21),
    .in22(RegData22), .in23(RegData23), .in24(RegData24), .in25(RegData25), .in26(RegData26),
    .in27(RegData27), .in28(RegData28), .in29(RegData29), .in30(RegData30), .in31(RegData31),
    .out(multiplexer_1_out), .sel(RdAddr1));
  Multiplexer #(.select(5), .width(32), .enable("false")) multiplexer_2 (
    .in0({32{1'b0}}), .in1(RegData1), .in2(RegData2), .in3(RegData3), .in4(RegData4), .in5(RegData5),
    .in6(RegData6), .in7(RegData7), .in8(RegData8), .in9(RegData9), .in10(RegData10), .in11(RegData11),
    .in12(RegData12), .in13(RegData13), .in14(RegData14), .in15(RegData15), .in16(RegData16),
    .in17(RegData17), .in18(RegData18), .in19(RegData19), .in20(RegData20), .in21(RegData21),
    .in22(RegData22), .in23(RegData23), .in24(RegData24), .in25(RegData25), .in26(RegData26),
    .in27(RegData27), .in28(RegData28), .in29(RegData29), .in30(RegData30), .in31(RegData31),
    .out(multiplexer_2_out), .sel(RdAddr2));
  Multiplexer #(.width(32), .enable("false")) multiplexer_3 (
    .in0(multiplexer_1_out), .in1(WrData), .out(RdData1), .sel(and_1_out));
  Multiplexer #(.width(32), .enable("false")) multiplexer_4 (
    .in0(multiplexer_2_out), .in1(WrData), .out(RdData2), .sel(and_2_out));
  Comparator #(.width(5), .mode("unsigned")) comparator_1 (
    .a(WrAddr), .b(RdAddr1), .eq(comparator_1_eq));  // open: gt, lt
  and and_1 (and_1_out, comparator_1_eq, WrReg, not_1_out);
  Comparator #(.width(5), .mode("unsigned")) comparator_2 (
    .a(WrAddr), .b(RdAddr2), .eq(comparator_2_eq));  // open: gt, lt
  and and_2 (and_2_out, comparator_2_eq, WrReg, not_2_out);
  Comparator #(.width(5), .mode("unsigned")) comparator_3 (
    .a(WrAddr), .b({5{1'b0}}), .eq(comparator_3_eq));  // open: gt, lt
  not not_1 (not_1_out, comparator_3_eq);
  Comparator #(.width(5), .mode("unsigned")) comparator_4 (
    .a(WrAddr), .b({5{1'b0}}), .eq(comparator_4_eq));  // open: gt, lt
  not not_2 (not_2_out, comparator_4_eq);
endmodule

module Overflow (
  input  Add,
  input  Sub,
  input  ASign,
  input  BSign,
  input  ResultSign,
  output Overflow
);

  wire and_1_out, and_2_out, or_1_out, xnor_1_out, xor_1_out, xor_2_out;

  xnor xnor_1 (xnor_1_out, ASign, BSign);
  xor xor_1 (xor_1_out, ASign, BSign);
  and and_1 (and_1_out, xnor_1_out, Add);
  and and_2 (and_2_out, xor_1_out, Sub);
  or or_1 (or_1_out, and_1_out, and_2_out);
  xor xor_2 (xor_2_out, ResultSign, ASign);
  and and_3 (Overflow, or_1_out, xor_2_out);

  // Notes on the sheet:
  //   Overflow occurs when doing addition and sign(A) == sign(B) && sign(result) != sign(A)
  //   Or
  //   Overflow occurs when doing subtraction and sign(A) != sign(B) && sign(result) != sign(A)
endmodule

module ALUControl (
  input  [5:0] in_1,
  input  [5:0] in_2,
  input  [1:0] in_3,
  output [2:0] out_4,
  output out_5
);

  wire [2:0] Helper1_p2, Helper2_p2;

  // Lab3_JonathanNguyen_SherrieShan_ALUControlHelper1 Helper1: pin names not known; wires that end beside it: in_2, Helper1_p2
  // Lab3_JonathanNguyen_SherrieShan_ALUControlHelper2 Helper2: pin names not known; wires that end beside it: in_1, Helper2_p2
  Comparator #(.width(6), .mode("unsigned")) comparator_1 (.a(in_2), .b(6'b001000), .eq(out_5));  // open: gt, lt
  Multiplexer #(.select(2), .width(3)) multiplexer_1 (
    .in0(3'b100), .in1(3'b001), .in2(Helper1_p2), .in3(Helper2_p2), .out(out_4), .sel(in_3));  // open: en

  // Other names for the same wires on the sheet: ALUControlBits[2:0] = out_4; Function[5:0] = in_2;
  //   Opcode[5:0] = in_1; Select[1:0] = in_3

  // Notes on the sheet:
  //   LW/SW
  //   R-type
  //   I-type
  //   BEQ
endmodule

module ALUControlHelper1 (
  input  [5:0] in_1,
  output [2:0] out_2
);

  wire and_1_out, and_2_out, and_3_out, and_4_out, and_5_out, and_6_out, not_1_out, not_2_out, not_3_out,
       not_4_out, not_5_out, not_6_out, not_7_out, not_8_out, not_9_out;

  not not_1 (not_1_out, in_1[5]);
  not not_2 (not_2_out, in_1[2]);
  and and_1 (and_1_out, not_2_out, not_3_out);
  not not_3 (not_3_out, in_1[1]);
  not not_4 (not_4_out, in_1[1]);
  and and_2 (and_2_out, not_4_out, in_1[0]);
  not not_5 (not_5_out, in_1[5]);
  and and_3 (and_3_out, in_1[2], not_6_out);
  not not_6 (not_6_out, in_1[0]);
  and and_4 (and_4_out, in_1[2], in_1[1]);
  not not_7 (not_7_out, in_1[3]);
  and and_5 (and_5_out, not_7_out, not_8_out, in_1[1]);
  not not_8 (not_8_out, in_1[2]);
  and and_6 (and_6_out, in_1[2], not_9_out);
  not not_9 (not_9_out, in_1[1]);
  or or_1 (out_2[2], not_1_out, and_1_out, and_2_out);
  or or_2 (out_2[1], not_5_out, and_3_out, and_4_out);
  or or_3 (out_2[0], and_5_out, and_6_out);

  // Other names for the same wires on the sheet: f0 = in_1[0]; f1 = in_1[1]; f2 = in_1[2]; f3 = in_1[3]; f4 = in_1[4];
  //   f5 = in_1[5]
endmodule

module ALUControlHelper2 (
  input  [5:0] in_1,
  output [2:0] out_2
);

  wire not_1_out, not_2_out;

  not not_1 (not_1_out, in_1[2]);
  not not_2 (not_2_out, in_1[0]);
  or or_1 (out_2[2], not_1_out, in_1[0]);
  and and_1 (out_2[1], in_1[2], not_2_out);

  assign out_2[0] = in_1[2];

  // Other names for the same wires on the sheet: o0 = in_1[0]; o1 = in_1[1]; o3 = in_1[3]; o4 = in_1[4]; o5 = in_1[5];
  //   o2 = in_1[2]
endmodule

module FwdControl (
  input  [4:0] in_1,
  input  in_2,
  input  [4:0] in_3,
  input  [4:0] in_4,
  input  [4:0] in_5,
  input  in_6,
  output [1:0] out_7,
  output [1:0] out_8
);

  wire comparator_1_eq, comparator_2_eq, comparator_3_eq, comparator_4_eq, comparator_5_eq, comparator_6_eq,
       comparator_7_eq, comparator_8_eq, not_1_out, not_2_out, not_3_out, not_4_out;
  wire [1:0] and_2_out, and_4_out;
  wire [4:0] xor_1_out, xor_2_out, xor_3_out, xor_4_out;

  assign xor_1_out = in_4 ^ in_1;  // XOR_Gate xor_1, 5 bits wide
  assign xor_2_out = in_5 ^ in_1;  // XOR_Gate xor_2, 5 bits wide
  assign xor_3_out = in_4 ^ in_3;  // XOR_Gate xor_3, 5 bits wide
  assign xor_4_out = in_5 ^ in_3;  // XOR_Gate xor_4, 5 bits wide
  Comparator #(.width(5)) comparator_1 (.a(xor_1_out), .b({5{1'b0}}), .eq(comparator_1_eq));  // open: gt, lt
  Comparator #(.width(5)) comparator_2 (.a(in_4), .b({5{1'b0}}), .eq(comparator_2_eq));  // open: gt, lt
  not not_1 (not_1_out, comparator_2_eq);
  Comparator #(.width(5)) comparator_3 (.a(xor_2_out), .b({5{1'b0}}), .eq(comparator_3_eq));  // open: gt, lt
  not not_2 (not_2_out, comparator_4_eq);
  Comparator #(.width(5)) comparator_4 (.a(in_5), .b({5{1'b0}}), .eq(comparator_4_eq));  // open: gt, lt
  Comparator #(.width(5)) comparator_5 (.a(xor_3_out), .b({5{1'b0}}), .eq(comparator_5_eq));  // open: gt, lt
  Comparator #(.width(5)) comparator_6 (.a(in_4), .b({5{1'b0}}), .eq(comparator_6_eq));  // open: gt, lt
  not not_3 (not_3_out, comparator_6_eq);
  Comparator #(.width(5)) comparator_7 (.a(xor_4_out), .b({5{1'b0}}), .eq(comparator_7_eq));  // open: gt, lt
  Comparator #(.width(5)) comparator_8 (.a(in_5), .b({5{1'b0}}), .eq(comparator_8_eq));  // open: gt, lt
  and and_1 (and_2_out[1], in_2, comparator_1_eq, not_1_out);
  and and_2 (and_2_out[0], in_6, comparator_3_eq, not_2_out);
  and and_3 (and_4_out[1], in_2, comparator_5_eq, not_3_out);
  and and_4 (and_4_out[0], in_6, comparator_7_eq, not_4_out);
  not not_4 (not_4_out, comparator_8_eq);
  Multiplexer #(.select(2), .width(2)) multiplexer_1 (
    .in0(2'b00), .in1(2'b10), .in2(2'b01), .in3(2'b01), .out(out_7), .sel(and_2_out));  // open: en
  Multiplexer #(.select(2), .width(2)) multiplexer_2 (
    .in0(2'b00), .in1(2'b10), .in2(2'b01), .in3(2'b01), .out(out_8), .sel(and_4_out));  // open: en

  // Other names for the same wires on the sheet: A_Select[1:0] = out_7; B_Select[1:0] = out_8; EX_RegDst[4:0] = in_4;
  //   EX_RegWrt = in_2; M_RegDst[4:0] = in_5; M_RegWrt = in_6; Rs[4:0] = in_1; Rt[4:0] = in_3
endmodule

module MFwdControl (
  input  [1:0] in_1,
  input  in_2,
  input  [4:0] in_3,
  input  [4:0] in_4,
  input  [4:0] in_5,
  input  [5:0] in_6,
  output out_7
);

  wire and_1_out, and_2_out, and_3_out, and_4_out, comparator_1_eq, comparator_2_eq, comparator_3_eq,
       comparator_4_eq, comparator_5_eq, or_1_out;

  Comparator #(.width(6)) comparator_1 (.a(in_6), .b({6{1'b0}}), .eq(comparator_1_eq));  // open: gt, lt
  Comparator #(.width(5)) comparator_2 (.a(in_3), .b(in_5), .eq(comparator_2_eq));  // open: gt, lt
  Comparator #(.width(3)) comparator_3 (.a(in_6[5:3]), .b(3'b001), .eq(comparator_3_eq));  // open: gt, lt
  Comparator #(.width(5)) comparator_4 (.a(in_4), .b(in_5), .eq(comparator_4_eq));  // open: gt, lt
  and and_1 (and_1_out, comparator_1_eq, comparator_2_eq);
  or or_1 (or_1_out, and_1_out, and_2_out);
  and and_2 (and_2_out, comparator_3_eq, comparator_4_eq);
  Comparator #(.width(5)) comparator_5 (.a(in_4), .b(in_5), .eq(comparator_5_eq));  // open: gt, lt
  and and_3 (and_3_out, in_2, or_1_out);
  and and_4 (and_4_out, in_1[0], comparator_5_eq);
  or or_2 (out_7, and_3_out, and_4_out);

  // Other names for the same wires on the sheet: DataSelect = out_7; EX_Rt[4:0] = in_5; M_MemtoReg[1:0] = in_1;
  //   M_Rd[4:0] = in_3; M_RegWrt = in_2; M_Rt[4:0] = in_4; opcode[5:0] = in_6
endmodule

module HazardDetection (
  input  in_1,
  input  [4:0] in_2,
  input  [4:0] in_3,
  input  [4:0] in_4,
  input  in_5,
  input  in_6,
  input  in_7,
  input  in_8,
  output out_9,
  output out_10,
  output out_11,
  output out_12
);

  wire comparator_1_eq, comparator_2_eq, comparator_3_eq, not_1_out, or_1_out, or_2_out;

  not not_1 (not_1_out, comparator_1_eq);
  Comparator #(.width(5)) comparator_1 (.a(in_3), .b({5{1'b0}}), .eq(comparator_1_eq));  // open: gt, lt
  Comparator #(.width(5)) comparator_2 (.a(in_3), .b(in_2), .eq(comparator_2_eq));  // open: gt, lt
  Comparator #(.width(5)) comparator_3 (.a(in_3), .b(in_4), .eq(comparator_3_eq));  // open: gt, lt
  or or_1 (or_1_out, comparator_2_eq, comparator_3_eq);
  or or_2 (or_2_out, in_6, in_7);
  and and_1 (out_9, in_1, not_1_out, or_1_out, or_2_out, in_8);
  or or_3 (out_11, out_9, in_5);
  // OR_Gate or_4 is placed but not wired

  assign out_10 = out_9;
  assign out_12 = in_5;

  // Other names for the same wires on the sheet: Bubble = out_11; clock = in_8; D_MemRead = in_6; D_Rs[4:0] = in_2;
  //   D_Rt[4:0] = in_4; Clear_Decode = in_5; EX_J_B = in_5; EX_MemRead = in_1; EX_Rt[4:0] = in_3; Jump = in_7;
  //   F_D_Write = out_9; PC_Write = out_9
endmodule
